# Fritzing sketch Arduino_Ag1170 (saved by Fritzing 0.3.19b)

parts:
  SilverTel_AG1170-S51 = SilverTel AG1170-S5
  Arduino1 = Arduino  # not connected
  D1 = Rectifier Diode
  D1_2 = Rectifier Diode
  D1_3 = Rectifier Diode
  D1_4 = Rectifier Diode

nets:
  N1: SilverTel_AG1170-S51.connector0, D1.connector1, D1_2.connector0
  N2: SilverTel_AG1170-S51.connector1, D1_3.connector0, D1_4.connector1
